# Fritzing sketch ADXL335 (saved by Fritzing 0.9.3b)
breadboards: 1

parts:
  Part1 = Arduino Nano (Rev3.0) (ICSP)
  Part2 = Triple Axis Accelerometer Breakout - ADXL335

nets:
  GND: Part1.GND, Part2.GND
  5V: Part1.5V, Part2.VCC
  N1: Part1.A2, Part2.ZOUT
  N2: Part1.A1, Part2.YOUT
  N3: Part1.A0, Part2.XOUT
  N4: Part1.AREF, Part1.3V3
