# Fritzing sketch ADXL335_calibration (saved by Fritzing 0.9.3b)
breadboards: 1

parts:
  Part1 = Arduino Nano (Rev3.0) (ICSP)
  Part2 = Triple Axis Accelerometer Breakout - ADXL335
  S1 = Pushbutton [package="[THT]"]
  R1 = Resistor [tolerance=±5% resistance=220 package=THT]

nets:
  N1: Part1.D2, S1.Pin_3, S1.Pin_4, R1.Pin_1
  GND: Part1.GND, Part2.GND, S1.Pin_1, S1.Pin_2
  5V: Part1.5V, Part2.VCC, R1.Pin_0
  N2: Part1.A2, Part2.ZOUT
  N3: Part1.A1, Part2.YOUT
  N4: Part1.A0, Part2.XOUT
  N5: Part1.AREF, Part1.3V3
