# Fritzing sketch BME680 (saved by Fritzing 0.9.3b)

parts:
  Part1 = Arduino Nano (Rev3.0) (ICSP)
  Part2 = Adafruit BME680 [part_number="Adafruit #3660"]

nets:
  GND: Part1.GND, Part2.GND
  5V: Part1.5V, Part2.VCC
  N1: Part1.A5, Part2.SCK/SCL
  N2: Part1.A4, Part2.SDI/SDA
