# Fritzing sketch BME680_SPI (saved by Fritzing 0.9.3b)

parts:
  Part1 = Arduino Nano (Rev3.0) (ICSP)
  Part2 = Adafruit BME680 [part_number="Adafruit #3660"]

nets:
  N1: Part1.D10, Part2.CS
  N2: Part1.D11/MOSI, Part2.SDI/SDA
  N3: Part1.D12/MISO, Part2.SDO/ADR
  GND: Part1.GND, Part2.GND
  5V: Part1.5V, Part2.VCC
  N4: Part1.D13/SCK, Part2.SCK/SCL
