# Fritzing sketch bmp180 (saved by Fritzing 0.9.3b)

parts:
  Part1 = Arduino Nano (Rev3.0)
  Part2 = Barometric Pressure Sensor - BMP180 Breakout (GY-68)

nets:
  GND: Part1.GND, Part2.GND
  5V: Part1.5V, Part2.VCC
  N1: Part1.A5, Part2.SCL
  N2: Part1.A4, Part2.SDA
