# Fritzing sketch MQ2gassensorLCD (saved by Fritzing 0.9.3b)
breadboards: 1

parts:
  Part1 = Arduino Nano (Rev3.0)
  J1 = Piezo Speaker
  R3 = Resistor [tolerance=±5% resistance=220 package="2010 [SMD]"]
  U1 = GAS_SENSOR [package=mq-3]
  LCD1 = LCD screen  # not connected

nets:
  N1: Part1.GND, R3.Pin_1, U1.A1
  N2: Part1.D10, J1.pin2
  N3: Part1.5V, U1.B1
  N4: J1.pin1, R3.Pin_0
  N5: U1.H1, U1.H2
