# Fritzing sketch MQ2gassensor (saved by Fritzing 0.9.3b)
breadboards: 1

parts:
  Part1 = Arduino Nano (Rev3.0)
  LED1 = smd LED [color="Red (633nm)" package="0805 [SMD]"]
  LED2 = smd LED [color="Green (565nm)" package="0805 [SMD]"]
  R1 = Resistor [tolerance=±5% resistance=220 package="2010 [SMD]"]
  R2 = Resistor [tolerance=±5% resistance=220 package="2010 [SMD]"]
  J1 = Piezo Speaker
  R3 = Resistor [tolerance=±5% resistance=220 package="2010 [SMD]"]
  U1 = GAS_SENSOR [package=mq-3]

nets:
  N1: Part1.GND, R1.Pin_1, R2.Pin_1, R3.Pin_1, U1.A1
  N2: Part1.D10, J1.pin2
  N3: Part1.D11/MOSI, LED2.anode
  N4: Part1.D12/MISO, LED1.anode
  N5: Part1.5V, U1.B1
  N6: LED1.cathode, R1.Pin_0
  N7: LED2.cathode, R2.Pin_0
  N8: J1.pin1, R3.Pin_0
  N9: U1.H1, U1.H2
