# Fritzing sketch MQ3sensor (saved by Fritzing 0.9.3b)

parts:
  Part1 = Arduino Nano (Rev3.0) (ICSP)
  U1 = GAS_SENSOR [package=mq-3]

nets:
  N1: Part1.GND, U1.H1
  N2: Part1.5V, U1.H2
  N3: Part1.A0, U1.B1
