# Fritzing sketch KY38sensor (saved by Fritzing 0.9.3b)
breadboards: 1

parts:
  Part1 = Arduino Nano (Rev3.0) (ICSP)
  LED1 = smd LED [color="Red (633nm)" package="0805 [SMD]"]
  R1 = Resistor [tolerance=±5% resistance=220 package="0402 [SMD]"]

nets:
  N1: Part1.GND, R1.Pin_0
  N2: Part1.D13/SCK, LED1.anode
  N3: LED1.cathode, R1.Pin_1
