# Fritzing sketch WTV020SD (saved by Fritzing 0.9.3b)
breadboards: 1

parts:
  Part1 = Arduino Nano (Rev3.0) (ICSP)
  S1 = Pushbutton [package="[THT]"]
  S2 = Pushbutton [package="[THT]"]
  S3 = Pushbutton [package="[THT]"]
  LED1 = LED - 5mm [color="Red (633nm)" package="5 mm [THT]"]
  R1 = Resistor [tolerance=±5% resistance=470 package="0402 [SMD]"]
  ADC1 = MCP3008 [package=dil16]
  SP1 = SPEAKER [package=pcb_mount_speaker]

nets:
  N1: Part1.D2, ADC1.CH0
  N2: Part1.D3, ADC1.CH6
  N3: Part1.D4, ADC1.CS/SHDN
  N4: Part1.D5, LED1.cathode, ADC1.VREF
  N5: Part1.GND, S1.Pin_1, S1.Pin_2, S2.Pin_1, S2.Pin_2, S3.Pin_1, S3.Pin_2, ADC1.CH7
  3V3: Part1.3V3, R1.Pin_1, ADC1.VDD
  N6: S1.Pin_3, S1.Pin_4, ADC1.CLK
  N7: S2.Pin_3, S2.Pin_4, ADC1.Dout
  N8: S3.Pin_3, S3.Pin_4, ADC1.DGND
  N9: LED1.anode, R1.Pin_0
  N10: ADC1.CH3, SP1.-
  N11: ADC1.CH4, SP1.+
